# Fritzing sketch ControlUnit Sheild for MegaPro RoboDyn EVNikolaProject PCB (saved by Fritzing 0.9.3b)
circuit board: 10.9594cm x 8.48873cm
breadboards: 1

parts:
  D1 = Rectifier Diode [part_number=1N4001 package="300 mil [THT]"]
  GND = JST-VHR-3N [part_number=JST-VHR-3N package=THT]
  GND_2 = JST-VHR-3N [part_number=JST-VHR-3N package=THT]
  Q1 = MOSFET-NCHANNEL [package=to220v]
  Q2 = MOSFET-NCHANNEL [package=to220v]
  IRF3205 = MOSFET-NCHANNEL [package=to220v]
  R1 = Resistor [tolerance=±5% resistance=220 package=THT]
  R2 = Resistor [tolerance=±5% resistance=220 package=THT]
  R3 = Resistor [tolerance=±5% resistance=220 package=THT]
  800mA = Fuse with Handler [part_number=Htc-15m]
  R4 = Resistor [tolerance=±5% resistance=81k package=THT]
  R5 = Resistor [tolerance=±5% resistance=8.2k package=THT]
  C1 = Ceramic Capacitor [capacitance=100nF package="200 mil [THT, multilayer]"]
  D2 = Rectifier Diode [part_number=1N4001 package="300 mil [THT]"]
  D3 = Rectifier Diode [part_number=1N4001 package="300 mil [THT]"]
  D4 = Rectifier Diode [part_number=1N4001 package="300 mil [THT]"]
  7808 = MOSFET-NCHANNEL [package=to220v]
  C2 = Ceramic Capacitor [capacitance=100nF package="200 mil [THT, multilayer]"]
  C3 = Ceramic Capacitor [capacitance=100nF package="200 mil [THT, multilayer]"]

nets:
  N1: D1.cathode, D2.cathode, D3.cathode, D4.cathode
  N2: GND.pin1, GND.pin_4, GND_2.pin1, GND_2.pin_4, R5.Pin_1, C1.1, 7808.D, C2.1, C3.0
  N3: Q1.G, R2.Pin_1
  N4: Q1.D, Q2.D, IRF3205.D, R4.Pin_1
  N5: Q2.G, R1.Pin_1
  N6: IRF3205.G, R3.Pin_1
  N7: 800mA.Connector1, 7808.G, C2.0
  N8: R4.Pin_0, R5.Pin_0, C1.0, D2.anode
  N9: 7808.S, C3.1

notes:
  I2C(Nano)
  UART(Nextion)
  WH.SW1
  WH.SW2
  uSW4
  SW3
  SW4
  Res. 5k (8+GND)
  Res. 5k (4+GND)
  2pSW
  uSW1
  uSW2
  SW2
  uSW3
  SW1
  uSW5
  5V
  OUTPUT to 16-channel 12V Relay
  PWM
  DIM
  Battery
  temp
  probe
  Pack
  Voltage
  Fuel g.
  Temp g.
  Dash lights
  elec3go institute slovenia
  MEGA 2560 PRO
  Extension board
  for EV Nikola
  16
  17
  20
  21
